# Fritzing sketch branchements fritzing (saved by Fritzing 0.9.3b)
breadboards: 2

parts:
  LCD1 = LCD screen
  R1 = Resistor [tolerance=±5% resistance=10k package=THT]
  R2 = Resistor [tolerance=±5% resistance=10k package=THT]
  R3 = Resistor [tolerance=±5% resistance=10k package=THT]
  R4 = Resistor [tolerance=±5% resistance=10k package=THT]
  R5 = Resistor [tolerance=±5% resistance=220 package=THT]
  S1 = Pushbutton [package="[THT]"]
  S2 = Pushbutton [package="[THT]"]
  S3 = Pushbutton [package="[THT]"]
  S4 = Pushbutton [package="[THT]"]
  Raspberry_Pi_1 = Raspberry Pi 3 [part_number=RPI-3-V1.2]
  Pololu_A1 = Pololu A4988 [package=SO16]
  M1 = Stepper Motor - Bipolar
  J1 = Power Jack [package=power_jack_pth_lock]
  Part1 = HX711 Weighing Sensor Module
  RHT1 = Humidity and Temperature Sensor RHT03

nets:
  VSS: LCD1.VSS, LCD1.R/W, LCD1.LED-, R5.Pin_1, S1.Pin_1, S1.Pin_2, S2.Pin_1, S2.Pin_2, S3.Pin_1, S3.Pin_2, S4.Pin_1, S4.Pin_2, Pololu_A1.GND#8, Part1.GND
  VDD: LCD1.VDD, LCD1.LED+, R1.Pin_1, R2.Pin_1, R3.Pin_1, R4.Pin_1, Pololu_A1.VDD
  N1: LCD1.V0, R5.Pin_0
  N2: LCD1.RS, Raspberry_Pi_1.GPIO17
  N3: LCD1.E, Raspberry_Pi_1.GPIO27
  N4: LCD1.DB4, Raspberry_Pi_1.GPIO22
  N5: LCD1.DB5, Raspberry_Pi_1.GPIO23
  N6: LCD1.DB6, Raspberry_Pi_1.GPIO24
  N7: LCD1.DB7, Raspberry_Pi_1.GPIO25
  N8: R1.Pin_0, S1.Pin_3, S1.Pin_4, Raspberry_Pi_1.GPIO6
  N9: R2.Pin_0, S2.Pin_3, S2.Pin_4, Raspberry_Pi_1.GPIO26
  N10: R3.Pin_0, S3.Pin_3, S3.Pin_4, Raspberry_Pi_1.GPIO19
  N11: R4.Pin_0, S4.Pin_3, S4.Pin_4, Raspberry_Pi_1.GPIO13
  3V3: Raspberry_Pi_1.3v3, Part1.VCC
  N12: Raspberry_Pi_1.GPIO5, Part1.DO/RX
  N13: Raspberry_Pi_1.GPIO21, Pololu_A1.DIR
  N14: Raspberry_Pi_1.GPIO20, Pololu_A1.STEP
  N15: Raspberry_Pi_1.GPIO16, Part1.CK/TX
  N16: Raspberry_Pi_1.GND, Pololu_A1.MS3
  N17: Raspberry_Pi_1.GPIO15, Pololu_A1.MS2
  N18: Raspberry_Pi_1.GPIO14, Pololu_A1.MS1
  N19: Pololu_A1.RESET, Pololu_A1.SLEEP
  N20: Pololu_A1.1B, M1.B
  N21: Pololu_A1.1A, M1.D
  N22: Pololu_A1.2A, M1.C
  N23: Pololu_A1.2B, M1.A
  N24: Pololu_A1.GND#14, J1.GND
  N25: Pololu_A1.VMOT, J1.PWR
  N26: Part1.A+, RHT1.GND_1
  N27: Part1.A-, RHT1.Vcc
  N28: Part1.B+, RHT1.Data-signal
  N29: Part1.B-, RHT1.GND_2
